// Logisim project CascadingAndComparator.circ as structural Verilog: 2 circuits, main circuit main
module main (
  input  High_bits,
  input  in_2,
  input  in_3,
  input  in_4,
  input  in_5,
  input  in_6,
  input  in_7,
  input  in_8
);

  wire node_1_equals, node_1_lessthan, node_2_equals, node_2_lessthan, node_3_equals, node_3_lessthan,
       node_4_equals, node_4_lessthan, or_1_out;

  Node node_1 (.Store(High_bits), .Measure(in_5), .Channel(1'b1), .Equals(node_1_equals), .LessThan(node_1_lessthan));
  Node node_2 (
    .Store(in_2), .Measure(in_6), .Channel(node_1_equals), .Equals(node_2_equals), .LessThan(node_2_lessthan));
  or or_1 (or_1_out, node_1_lessthan, node_2_lessthan, node_3_lessthan, node_4_lessthan);
  Node node_3 (
    .Store(in_3), .Measure(in_7), .Channel(node_2_equals), .Equals(node_3_equals), .LessThan(node_3_lessthan));
  Node node_4 (
    .Store(in_4), .Measure(in_8), .Channel(node_3_equals), .Equals(node_4_equals), .LessThan(node_4_lessthan));
  LED led_1 (.in(node_4_equals));
  LED led_2 (.in(or_1_out));

  // Notes on the sheet:
  //   Cascading And Comparator
  //   Upper Number
  //   Equal
  //   Lower Number
  //   Less Than
endmodule

module Node (
  input  Store,
  input  Measure,
  input  Channel,
  output Equals,
  output LessThan
);

  wire not_1_out, xnor_1_out;

  not not_1 (not_1_out, Measure);
  xnor xnor_1 (xnor_1_out, Store, Measure);
  and eq (Equals, xnor_1_out, Channel);
  and lt (LessThan, Store, not_1_out, Channel);

  // Notes on the sheet:
  //   Compare one pair of bits
endmodule
