// Logisim project Node2.circ as structural Verilog: 2 circuits, main circuit main
module main (
  input  High_bits,
  input  in_2,
  input  in_3,
  input  in_4,
  input  in_5,
  input  in_6,
  input  in_7,
  input  in_8
);

  wire and_1_out, and_2_out, and_3_out, and_4_out, node_1_channel2, node_2_channel2, node_3_channel2,
       node_4_channel2, not_1_out, not_2_out, not_3_out, not_4_out, or_1_out;

  Node node_1 (.Store(High_bits), .Measure(in_5), .Channel(1'b1), .Channel2(node_1_channel2));
  not not_1 (not_1_out, in_5);
  and and_1 (and_1_out, not_1_out, High_bits, 1'b1);
  Node node_2 (.Store(in_2), .Measure(in_6), .Channel(node_1_channel2), .Channel2(node_2_channel2));
  and and_2 (and_2_out, not_2_out, in_2, node_1_channel2);
  not not_2 (not_2_out, in_6);
  or or_1 (or_1_out, and_1_out, and_2_out, and_3_out, and_4_out);
  Node node_3 (.Store(in_3), .Measure(in_7), .Channel(node_2_channel2), .Channel2(node_3_channel2));
  not not_3 (not_3_out, in_7);
  and and_3 (and_3_out, not_3_out, in_3, node_2_channel2);
  Node node_4 (.Store(in_4), .Measure(in_8), .Channel(node_3_channel2), .Channel2(node_4_channel2));
  and and_4 (and_4_out, not_4_out, in_4, node_3_channel2);
  not not_4 (not_4_out, in_8);
  LED led_1 (.in(node_4_channel2));
  LED led_2 (.in(or_1_out));

  // Notes on the sheet:
  //   Sequential And Comparator
  //   Upper Number
  //   Equal
  //   Lower Number
  //   Less Than
endmodule

module Node (
  input  Store,
  input  Measure,
  input  Channel,
  output Channel2
);

  wire xnor_1_out;

  xnor xnor_1 (xnor_1_out, Store, Measure);
  and and_1 (Channel2, xnor_1_out, Channel);
endmodule
